// Logisim project CPU_RISCV.circ as structural Verilog
module main (
  input  [4:0] in_1,
  input  in_2
);

  wire alu_1_zero, and_1_out, clock_1_out, ex_mem_1_zeroout, multiplexer_4_out, not_1_out, or_2_out;
  wire [1:0] or_1_out, unidade_controle_1_aluop, unidade_controle_1_alusrc, unidade_controle_1_regsrc;
  wire [2:0] ex_mem_1_wbout, id_ex_1_p19, mem_wb_1_wbout;
  wire [2:2] unidade_controle_1_regwrite;
  wire [3:0] alu_controle_1_control, id_ex_1_p16, id_ex_1_p20, if_id_1_instout_6;
  wire [4:0] ex_mem_1_mout, ex_mem_1_wbaddout, id_ex_1_p17, if_id_1_instout_3, if_id_1_instout_4,
       if_id_1_instout_5, mem_wb_1_wbaddout;
  wire [5:0] id_ex_1_p18, unidade_controle_1_memread;
  wire [6:0] if_id_1_instout_2;
  wire [7:0] counter_1_q;
  wire [31:0] alu_1_resultado, ex_mem_1_aluout, ex_mem_1_pcout, ex_mem_1_pcpl4out, ex_mem_1_read2out,
       id_ex_1_p12, id_ex_1_p13, id_ex_1_p14, id_ex_1_p15, id_ex_1_p21, if_id_1_pcout, if_id_1_pcpl4out,
       imediato_1_imm, mem_wb_1_aluout, mem_wb_1_pcpl4out, mem_wb_1_pcpliout, mem_wb_1_readout,
       multiplexer_1_out, multiplexer_2_out, multiplexer_3_out, multiplexer_5_out, pc_1_pc_out, ram_1_dout,
       registrador_1_outregmanual, registrador_1_outx, registrador_1_outy, rom_1_data, somador_1_z,
       somador_2_z;
  wire [31:25] if_id_1_instout;

  Clock clock_1 (.out(clock_1_out));
  Counter counter_1 (.Q(counter_1_q), .clk(clock_1_out), .clr(in_2));  // open: load, D, count, carry, up
  PC pc_1 (.clk(counter_1_q[0]), .reset(in_2), .pc_in(multiplexer_1_out), .pc_out(pc_1_pc_out));
  ROM #(.addrWidth(24), .dataWidth(32)) rom_1 (.addr(pc_1_pc_out[23:0]), .data(rom_1_data));
  Somador somador_1 (.X(pc_1_pc_out), .Y(32'h1), .Z(somador_1_z));
  IF_ID if_id_1 (
    .clk(counter_1_q[0]), .pcIn(pc_1_pc_out), .pcPl4In(somador_1_z), .instIn(rom_1_data),
    .pcOut(if_id_1_pcout), .pcPl4Out(if_id_1_pcpl4out),
    .instOut({if_id_1_instout[31], if_id_1_instout_6[3], if_id_1_instout[29:25], if_id_1_instout_4, if_id_1_instout_3, if_id_1_instout_6[2:0], if_id_1_instout_5, if_id_1_instout_2}));
  // Probe on {if_id_1_instout[31], if_id_1_instout_6[3], if_id_1_instout[29:25], if_id_1_instout_4, if_id_1_instout_3, if_id_1_instout_6[2:0], if_id_1_instout_5, if_id_1_instout_2}
  // Probe on registrador_1_outregmanual
  Registrador registrador_1 (
    .\input (multiplexer_5_out), .regSelManual(in_1), .writeEnable(mem_wb_1_wbout[2]),
    .regXSel(if_id_1_instout_3), .regYSel(if_id_1_instout_4), .writeRegSel(mem_wb_1_wbaddout),
    .clk(clock_1_out), .outX(registrador_1_outx), .outY(registrador_1_outy),
    .outRegManual(registrador_1_outregmanual));
  Imediato imediato_1 (
    .inst({if_id_1_instout[31], if_id_1_instout_6[3], if_id_1_instout[29:25], if_id_1_instout_4, if_id_1_instout_3, if_id_1_instout_6[2:0], if_id_1_instout_5, if_id_1_instout_2}),
    .imm(imediato_1_imm));
  Unidade_Controle unidade_controle_1 (
    .opcode(if_id_1_instout_2), .AluSrc(unidade_controle_1_alusrc[0]), .blockA(unidade_controle_1_alusrc[1]),
    .RegWrite(unidade_controle_1_regwrite[2]), .MemRead(unidade_controle_1_memread[0]),
    .MemWrite(unidade_controle_1_memread[1]), .Branch(unidade_controle_1_memread[2]),
    .BranchNotEq(unidade_controle_1_memread[3]), .BrIncond(unidade_controle_1_memread[4]),
    .regToPC(unidade_controle_1_memread[5]), .AluOp(unidade_controle_1_aluop),
    .regSrc(unidade_controle_1_regsrc));
  Multiplexer #(.select(2), .width(32)) multiplexer_1 (
    .in0(somador_1_z), .in1(ex_mem_1_pcout), .in2(ex_mem_1_aluout), .in3(ex_mem_1_aluout),
    .out(multiplexer_1_out), .sel(or_1_out));  // open: en
  // Probe on imediato_1_imm
  // ID_EX id_ex_1: pin names not known; wires that end beside it: counter_1_q[0], if_id_1_pcout, registrador_1_outx, registrador_1_outy, imediato_1_imm, if_id_1_instout_6, if_id_1_instout_5, {unidade_controle_1_regwrite[2], unidade_controle_1_regsrc}, unidade_controle_1_memread, {unidade_controle_1_aluop, unidade_controle_1_alusrc}, if_id_1_pcpl4out, id_ex_1_p12, id_ex_1_p13, id_ex_1_p14, id_ex_1_p15, id_ex_1_p16, id_ex_1_p17, id_ex_1_p18, id_ex_1_p19, id_ex_1_p20, id_ex_1_p21
  Multiplexer #(.width(32)) multiplexer_2 (
    .in0(id_ex_1_p13), .in1({32{1'b0}}), .out(multiplexer_2_out), .sel(id_ex_1_p20[1]));  // open: en
  Multiplexer #(.width(32)) multiplexer_3 (
    .in0(id_ex_1_p14), .in1(id_ex_1_p15), .out(multiplexer_3_out), .sel(id_ex_1_p20[0]));  // open: en
  ALU_Controle alu_controle_1 (.Functs(id_ex_1_p16), .AluOp(id_ex_1_p20[3:2]), .control(alu_controle_1_control));
  Somador somador_2 (.X(id_ex_1_p12), .Y(id_ex_1_p15), .Z(somador_2_z));
  ALU alu_1 (
    .X(multiplexer_2_out), .Y(multiplexer_3_out), .control(alu_controle_1_control),
    .resultado(alu_1_resultado), .zero(alu_1_zero));
  EX_MEM ex_mem_1 (
    .clk(counter_1_q[0]), .sumIn(somador_2_z), .zeroIn(alu_1_zero), .aluIn(alu_1_resultado),
    .read2In(id_ex_1_p14), .wbAddIn(id_ex_1_p17), .WBin(id_ex_1_p19), .Min(id_ex_1_p18),
    .pcPl4In(id_ex_1_p21), .pcOut(ex_mem_1_pcout), .zeroOut(ex_mem_1_zeroout), .aluOut(ex_mem_1_aluout),
    .read2Out(ex_mem_1_read2out), .wbAddOut(ex_mem_1_wbaddout), .WBout(ex_mem_1_wbout),
    .Mout({or_1_out[1], ex_mem_1_mout}), .pcPl4Out(ex_mem_1_pcpl4out));
  or or_1 (or_1_out[0], ex_mem_1_mout[4], and_1_out);
  and and_1 (and_1_out, or_2_out, multiplexer_4_out);
  or or_2 (or_2_out, ex_mem_1_mout[2], ex_mem_1_mout[3]);
  Multiplexer multiplexer_4 (
    .in0(ex_mem_1_zeroout), .in1(not_1_out), .out(multiplexer_4_out), .sel(ex_mem_1_mout[3]));  // open: en
  not not_1 (not_1_out, ex_mem_1_zeroout);
  RAM #(.addrWidth(24), .dataWidth(32)) ram_1 (
    .addr(ex_mem_1_aluout[23:0]), .we(ex_mem_1_mout[1]), .oe(ex_mem_1_mout[0]), .clk(clock_1_out),
    .din(ex_mem_1_read2out), .dout(ram_1_dout));
  MEM_WB mem_wb_1 (
    .clk(counter_1_q[0]), .readIn(ram_1_dout), .aluIn(ex_mem_1_aluout), .wbAddIn(ex_mem_1_wbaddout),
    .WBin(ex_mem_1_wbout), .pcPl4In(ex_mem_1_pcpl4out), .pcPlIIn(ex_mem_1_pcout), .readOut(mem_wb_1_readout),
    .aluOut(mem_wb_1_aluout), .wbAddOut(mem_wb_1_wbaddout), .WBout(mem_wb_1_wbout),
    .pcPl4Out(mem_wb_1_pcpl4out), .pcPlIOut(mem_wb_1_pcpliout));
  Multiplexer #(.select(2), .width(32)) multiplexer_5 (
    .in0(mem_wb_1_aluout), .in1(mem_wb_1_readout), .in2(mem_wb_1_pcpl4out), .in3(mem_wb_1_pcpliout),
    .out(multiplexer_5_out), .sel(mem_wb_1_wbout[1:0]));  // open: en

  // Notes on the sheet:
  //   contents of rom_1 (hex, n*v repeats v):
  //   9563
  //   1° Estágio do Pipeline
  //   Instruction Fetch
  //   2° Estágio do Pipeline
  //   Instruction Decode
  //   3° Estágio do Pipeline
  //   Execute
  //   4° Estágio do Pipeline
  //   Memory Access
  //   5° Estágio do Pipeline
  //   Write Back
endmodule

// VHDL entity ALU, as the project stores it:
library IEEE;
use IEEE.STD_LOGIC_1164.ALL;
use ieee.numeric_std.ALL;
USE IEEE.std_logic_unsigned.ALL;

entity ALU is
    port(
    X, Y      : in std_logic_vector(31 downto 0);
    control  : in std_logic_vector(3 downto 0);
    resultado : out std_logic_vector(31 downto 0);
    zero      : out std_logic);
end ALU;

architecture TypeArchitecture of ALU is

signal zero_out   : std_logic_vector(32 downto 0);
signal resultado_out : std_logic_vector(31 downto 0);


begin
	
    resultado_out <= (X + Y) when control = "0010" else
    			   (X AND Y) when control = "0000" else
    			   (X - Y) when control = "0110" else
    			   (X OR Y) when control = "0001" else
    			   (X XOR Y) when control = "0101" else
    			   (std_logic_vector(shift_left(unsigned(X), to_integer(unsigned(Y))))) when control = "0011" else
    			   (std_logic_vector(shift_right(unsigned(X), to_integer(unsigned(Y))))) when control = "0111";
        			
    resultado <= resultado_out;
    zero_out(0)<= '0';
    G: for I in 1 to 32 generate
            zero_out(I) <= zero_out(I - 1) or resultado_out(I - 1);
    end generate;
    zero <= not zero_out(32);
end TypeArchitecture;

// VHDL entity ALU_Controle, as the project stores it:
library IEEE;
use IEEE.STD_LOGIC_1164.ALL;

entity ALU_Controle is
    port(
        Functs    : IN std_logic_vector(3 downto 0);
        AluOp   : IN std_logic_vector(1 downto 0);
        control : OUT std_logic_vector(3 downto 0)
        );
end ALU_Controle;

architecture TypeArchitecture of ALU_Controle is
begin

	control <= "0010" when AluOp = "00" else -- l/w
			 "0110" when AluOp = "01" else -- Branch
			 "0010" when Functs = "0000" else -- Add
			 "0110" when Functs = "1000" else -- Sub
			 "0011" when Functs = "0001" else -- Shift left
			 "0101" when Functs = "0100" else -- Xor
			 "0111" when Functs = "0101" else -- Shift Right
			 "0001" when Functs = "0110" else -- Or
			 "0000" when Functs = "0111"; -- And			 
	
end TypeArchitecture;

// VHDL entity Unidade_Controle, as the project stores it:
library IEEE;
use IEEE.STD_LOGIC_1164.ALL;


entity Unidade_Controle is
    port(
        opcode                     : IN  std_logic_vector(6 downto 0);
        AluSrc, blockA, RegWrite 	: OUT std_logic;
        MemRead, MemWrite, Branch  : OUT std_logic;
        BranchNotEq, BrIncond		: OUT std_logic;
        regToPC 			     : OUT std_logic;
        AluOp,regSrc		     : OUT std_logic_vector(1 downto 0)
        );
end Unidade_Controle;

architecture TypeArchitecture of Unidade_Controle is

begin
	process(opcode)
	begin
		-- R-Type s/ imediato
	    	IF (opcode = "0110011") THEN
            AluSrc      <= '0';
            blockA      <= '0';
            RegWrite    <= '1';
            MemRead     <= '0';
            MemWrite    <= '0';
            Branch      <= '0';
            AluOp       <= "10";
            regSrc      <= "00";
            BranchNotEq <= '0';
            BrIncond    <= '0';
            regToPC     <= '0';
        END IF;

	   -- R-Type c/ imediato
        IF (opcode = "0010011") THEN
            AluSrc      <= '1';
            blockA      <= '0';
            RegWrite    <= '1';
            MemRead     <= '0';
            MemWrite    <= '0';
            Branch      <= '0';
            AluOp       <= "11";
            regSrc      <= "00";
            BranchNotEq <= '0';
            BrIncond    <= '0';
            regToPC     <= '0';
        END IF;
        
        -- jalr (jump registrador)
	   IF (opcode = "1100110") THEN
            AluSrc      <= '1';
            blockA      <= '0';
            RegWrite    <= '1';
            MemRead     <= '0';
            MemWrite    <= '0';
            Branch      <= '0';
            AluOp       <= "00";
            regSrc      <= "10";
            BranchNotEq <= '0';
            BrIncond    <= '1';
            regToPC     <= '1';
        END IF;
        
	   -- jal (jump PC)
	   IF (opcode = "1101111") THEN
            AluSrc      <= '1';
            blockA      <= '0';
            RegWrite    <= '1';
            MemRead     <= '0';
            MemWrite    <= '0';
            Branch      <= '0';
            AluOp       <= "00";
            regSrc      <= "10";
            BranchNotEq <= '0';
            BrIncond    <= '1';
            regToPC     <= '0';
        END IF;

        -- lw (load registrador)
        IF (opcode = "0000011") THEN
            AluSrc      <= '1';
            blockA      <= '0';
            RegWrite    <= '1';
            MemRead     <= '1';
            MemWrite    <= '0';
            Branch      <= '0';
            AluOp       <= "00";
            regSrc      <= "01";
            BranchNotEq <= '0';
            BrIncond    <= '0';
            regToPC     <= '0';
        END IF;

	   -- lui (load imediato)
        IF (opcode = "0110111") THEN
            AluSrc      <= '1';
            blockA      <= '1';
            RegWrite    <= '1';
            MemRead     <= '0';
            MemWrite    <= '0';
            Branch      <= '0';
            AluOp       <= "00";
            regSrc      <= "00";
            BranchNotEq <= '0';
            BrIncond    <= '0';
            regToPC     <= '0';
        END IF;        
	   -- sw (store)
        IF (opcode = "0100011") THEN
            AluSrc      <= '1';
            blockA      <= '0';
            RegWrite    <= '0';
            MemRead     <= '0';
            MemWrite    <= '1';
            Branch      <= '0';
            AluOp       <= "00";
            regSrc      <= "00";
            BranchNotEq <= '0';
            BrIncond    <= '0';
            regToPC     <= '0';
        END IF;

	   -- beq (branch if equal)
        IF (opcode = "1100111") THEN
            AluSrc      <= '0';
            blockA      <= '0';
            RegWrite    <= '0';
            MemRead     <= '0';
            MemWrite    <= '0';
            Branch      <= '1';
            AluOp       <= "01";
            regSrc      <= "00";
            BranchNotEq <= '0';
            BrIncond    <= '0';
            regToPC     <= '0';
        END IF;

	   -- bnq (branch not equal)
        IF (opcode = "1100011") THEN
            AluSrc      <= '0';
            blockA      <= '0';
            RegWrite    <= '0';
            MemRead     <= '0';
            MemWrite    <= '0';
            Branch      <= '0';
            AluOp       <= "01";
            regSrc      <= "00";
            BranchNotEq <= '1';
            BrIncond    <= '0';
            regToPC     <= '0';
        END IF;

	   -- auipc ( add imediato no PC)
        IF (opcode = "1110111") THEN
            AluSrc      <= '1';
            blockA      <= '0';
            RegWrite    <= '1';
            MemRead     <= '0';
            MemWrite    <= '0';
            Branch      <= '0';
            AluOp       <= "00";
            regSrc      <= "11";
            BranchNotEq <= '0';
            BrIncond    <= '1';
            regToPC     <= '0';
        END IF;
        
	end process;
end TypeArchitecture;

// VHDL entity Imediato, as the project stores it:
library IEEE;
use IEEE.STD_LOGIC_1164.ALL;
USE IEEE.NUMERIC_STD.ALL;

entity Imediato is
    Port( 
        inst: in std_logic_vector(31 downto 0);
        imm: out std_logic_vector(31 downto 0));
end Imediato;

architecture Behavioral of Imediato is
signal opcode		: std_logic_vector(6 downto 0);
signal imm_interno 	: std_logic_vector(31 downto 0) := "00000000000000000000000000000000";

begin

opcode <= inst(6 downto 0);

process(opcode)
begin
	--Tipo I
	if (opcode = "0010011" or opcode = "1100110") then
		imm_interno(11 downto 0)  <= inst(31 downto 20);
		imm_interno(31 downto 12) <= (others => inst(31));
		
	-- Tipo U	
	elsif (opcode = "1110111" or opcode = "0110111") then
		imm_interno(31 downto 12) <= inst(31 downto 12);
		
	-- Tipo S	
	elsif (opcode = "0100011") then
		imm_interno(11 downto 5) <= inst(31 downto 25);
		imm_interno(4 downto 0)  <= inst(11 downto 7);
		imm_interno(31 downto 12) <= (others => inst(31));
		
	-- Tipo SB	
	elsif (opcode = "1100111" or opcode = "1100011") then 
		imm_interno(12) <= inst(31);
		imm_interno(11) <= inst(7);
		imm_interno(10 downto 5) <= inst(30 downto 25);
		imm_interno(4 downto 1) <= inst(11 downto 8);
		imm_interno(31 downto 13) <= (others => inst(31));
		
	-- Tipo UJ	
	elsif (opcode = "1101111") then
		imm_interno(20) <= inst(31);
		imm_interno(19 downto 12) <= inst(19 downto 12);
		imm_interno(11) <= inst(20);
		imm_interno(10 downto 1) <= inst(30 downto 21);
	end if;
end process;

imm <= imm_interno;

end Behavioral;

// VHDL entity PC, as the project stores it:
LIBRARY IEEE;
USE ieee.std_logic_1164.all;

ENTITY PC IS
  PORT (
  ------------------------------------------------------------------------------

    clk      : IN  std_logic;
    reset    : IN  std_logic;
    pc_in    : IN  std_logic_vector(31 DOWNTO 0); 
  ------------------------------------------------------------------------------

    pc_out   : OUT std_logic_vector(31 DOWNTO 0)
    );
END PC;

ARCHITECTURE TypeArchitecture OF PC IS

BEGIN

	
	PROCESS (clk, reset)
	BEGIN
		IF (rising_edge(clk)) THEN
			if (pc_in = "UUUUUUUUUUUUUUUUUUUUUUUUUUUUUUUU") then
				pc_out <= (others => '0');
			else
				pc_out <= pc_in;
			end if;
		END IF;
		IF (reset = '1') THEN
			pc_out <= (others => '0');
		END IF;
	END PROCESS;

END TypeArchitecture;

// VHDL entity Somador, as the project stores it:
LIBRARY IEEE;
USE ieee.std_logic_1164.all;

USE IEEE.std_logic_unsigned.ALL;

ENTITY Somador IS
  PORT (
  ------------------------------------------------------------------------------
    X, Y        : IN  std_logic_vector(31 DOWNTO 0); -- entrada
  ------------------------------------------------------------------------------
    Z           : OUT std_logic_vector(31 DOWNTO 0)  -- saida
    );
END Somador;

ARCHITECTURE TypeArchitecture OF Somador IS

BEGIN

Z <= X + Y;

END TypeArchitecture;

// VHDL entity Registrador, as the project stores it:
library IEEE;
use ieee.std_logic_1164.all;
use ieee.numeric_std.all;

entity Registrador is
  port(
    outX        : out std_logic_vector(31 downto 0);
    outY        : out std_logic_vector(31 downto 0);
    input       : in  std_logic_vector(31 downto 0);
    regSelManual: in  std_logic_vector(4 downto 0);
    outRegManual: out std_logic_vector(31 downto 0);
    writeEnable : in  std_logic;
    regXSel     : in  std_logic_vector(4 downto 0);
    regYSel     : in  std_logic_vector(4 downto 0);
    writeRegSel : in  std_logic_vector(4 downto 0);
    clk         : in  std_logic
    );
end Registrador;


architecture TypeArchitecture of Registrador is
  type registerFile is array(0 to 31) of std_logic_vector(31 downto 0);
  signal registers : registerFile := 
   ("00000000000000000000000000010000","00000000000000000000000000000001","00000000000000000000000000000000","00000000000000000000000000000000",
    "00000000000000000000000000000000","00000000000000000000000000000000","00000000000000000000000000000000","00000000000000000000000000000000",
    "00000000000000000000000000000000","00000000000000000000000000000000","00000000000000000000000000000000","00000000000000000000000000000000",
    "00000000000000000000000000000000","00000000000000000000000000000000","00000000000000000000000000000000","00000000000000000000000000000000",
    "00000000000000000000000000000000","00000000000000000000000000000000","00000000000000000000000000000000","00000000000000000000000000000000",
    "00000000000000000000000000000000","00000000000000000000000000000000","00000000000000000000000000000000","00000000000000000000000000000000",
    "00000000000000000000000000000000","00000000000000000000000000000000","00000000000000000000000000000000","00000000000000000000000000000000",
    "00000000000000000000000000000000","00000000000000000000000000000000","00000000000000000000000000000000","00000000000000000000000000000000");
begin
regFile : process (clk) is
  begin
    if rising_edge(clk) then
      -- Read A and B before bypass
      if (registers(to_integer(unsigned(regXSel))) = "UUUUUUUUUUUUUUUUUUUUUUUUUUUUUUUU") THEN
      	outX <= (others => '0');
      ELSE 
      	outX <= registers(to_integer(unsigned(regXSel)));
      END IF;
      IF (registers(to_integer(unsigned(regYSel))) = "UUUUUUUUUUUUUUUUUUUUUUUUUUUUUUUU") THEN
      	outY <= (others => '0');
      ELSE
      	outY <= registers(to_integer(unsigned(regYSel)));
      END IF;
      -- Write and bypass
      if writeEnable = '1' then
        registers(to_integer(unsigned(writeRegSel))) <= input;  -- Write
        if regASel = writeRegSel then  -- Bypass for read A
          outX <= input;
        end if;
        if regBSel = writeRegSel then  -- Bypass for read B
          outY <= input;
        end if;
      end if;
    end if;
  end process;
  -- manual selection
  outRegManual <= registers(to_integer(unsigned(regSelManual)));
  
end TypeArchitecture;

// VHDL entity IF_ID, as the project stores it:
LIBRARY IEEE;
USE ieee.std_logic_1164.all;

ENTITY IF_ID IS
  PORT (
    clk         : IN  std_logic;                   
    pcIn        : IN  std_logic_vector(31 DOWNTO 0);
    pcPl4In	 : IN  std_logic_vector(31 downto 0);
    instIn      : IN  std_logic_vector(31 DOWNTO 0);
    pcOut       : OUT std_logic_vector(31 DOWNTO 0);   
    pcPl4Out	 : OUT std_logic_vector(31 downto 0);                 
    instOut     : OUT std_logic_vector(31 DOWNTO 0)
    );
END IF_ID;


ARCHITECTURE TypeArchitecture OF IF_ID IS

SIGNAL IDIF : std_logic_vector(95 DOWNTO 0);

BEGIN


	
	PROCESS (clk)
	BEGIN
		IF (rising_edge(clk)) THEN
			IDIF(31 DOWNTO 0) <= instIn;
			IDIF(63 DOWNTO 32) <= pcIn;
			IDIF(95 downto 64) <= pcPl4In;
		END IF;
		IF (falling_edge(clk)) THEN
			pcOut <= IDIF(63 DOWNTO 32);
			instOut <= IDIF(31 DOWNTO 0);
			pcPl4Out <= IDIF(95 downto 64);
		END IF;
	END PROCESS;

	
END TypeArchitecture;

// VHDL entity ID_EX, as the project stores it:
LIBRARY IEEE;
USE ieee.std_logic_1164.all;

ENTITY ID_EX IS
  PORT (
    clk            : IN  std_logic;                   
    pcIn           : IN  std_logic_vector(31 DOWNTO 0);
    read1In        : IN  std_logic_vector(31 DOWNTO 0);
    read2In        : IN  std_logic_vector(31 DOWNTO 0);
    immGenIn       : in  std_logic_vector(31 DOWNTO 0);
    aluControlin   : IN  std_logic_vector(3 downto 0);
    wbAddIn        : IN  std_logic_vector(4 downto 0);
    WBin		    : IN  std_logic_vector(2 downto 0);
    Min 		    : IN  std_logic_vector(5 downto 0);
    EXin    	    : IN  std_logic_vector(3 downto 0);
    pcPl4In	    : IN  std_logic_vector(31 downto 0);
                        
    pcOut          : OUT std_logic_vector(31 DOWNTO 0);
    read1Out	    : OUT std_logic_vector(31 DOWNTO 0);
    read2Out       : OUT std_logic_vector(31 DOWNTO 0);
    immGenOut      : OUT std_logic_vector(31 DOWNTO 0);
    aluControlout  : OUT std_logic_vector(3 downto 0);
    wbAddOut       : OUT std_logic_vector(4 downto 0);
    WBout		    : OUT std_logic_vector(2 downto 0);
    Mout 		    : OUT std_logic_vector(5 downto 0);
    EXout    	    : OUT std_logic_vector(3 downto 0);
    pcPl4Out	    : OUT std_logic_vector(31 downto 0)
    );
END ID_EX;


ARCHITECTURE TypeArchitecture OF ID_EX IS

SIGNAL idex_s : std_logic_vector(181 DOWNTO 0);

BEGIN

	PROCESS (clk)
	BEGIN
		IF (rising_edge(clk)) THEN
			idex_s(31 DOWNTO 0)    <= pcIn;
			idex_s(63 DOWNTO 32)   <= read1In;
			idex_s(95 DOWNTO 64)   <= read2In;
			idex_s(127 DOWNTO 96)  <= immGenIn;
			idex_s(131 DOWNTO 128) <= aluControlin;
			idex_s(136 DOWNTO 132) <= wbAddIn;
			idex_s(139 downto 137) <= WBin;
			idex_s(145 downto 140) <= Min;
			idex_s(149 downto 146) <= EXin;
			idex_s(181 downto 150) <= pcPl4In;
		END IF;
		IF (falling_edge(clk)) THEN
			pcOut    <= idex_s(31 DOWNTO 0);
			read1Out  <= idex_s(63 DOWNTO 32);
			read2Out  <= idex_s(95 DOWNTO 64);
			immGenOut <= idex_s(127 DOWNTO 96);
			aluControlout <= idex_s(131 DOWNTO 128);
			wbAddOut <= idex_s(136 DOWNTO 132);
			WBout <= idex_s(139 downto 137);
			Mout <= idex_s(145 downto 140);
			EXout <= idex_s(149 downto 146);
			pcPl4Out <= idex_s(181 downto 150);
		END IF;
	END PROCESS;

	
END TypeArchitecture;

// VHDL entity EX_MEM, as the project stores it:
LIBRARY IEEE;
USE ieee.std_logic_1164.all;

ENTITY EX_MEM IS
  PORT (
    clk            : IN  std_logic;                   
    sumIn           : IN  std_logic_vector(31 DOWNTO 0);
    zeroIn        : IN  std_logic;
    aluIn        : IN  std_logic_vector(31 DOWNTO 0);
    read2In       : in  std_logic_vector(31 DOWNTO 0);
    wbAddIn        : IN  std_logic_vector(4 downto 0);
    WBin		    : IN  std_logic_vector(2 downto 0);
    Min 		    : IN  std_logic_vector(5 downto 0);
    pcPl4In	    : IN std_logic_vector(31 downto 0);
    
                        
    pcOut         : OUT std_logic_vector(31 DOWNTO 0);
    zeroOut	    : OUT std_logic;
    aluOut       : OUT std_logic_vector(31 DOWNTO 0);
    read2Out      : OUT std_logic_vector(31 DOWNTO 0);
    wbAddOut       : OUT std_logic_vector(4 downto 0);
    WBout		    : OUT std_logic_vector(2 downto 0);
    Mout 		    : OUT std_logic_vector(5 downto 0);
    pcPl4Out	    : OUT std_logic_vector(31 downto 0)
    );
END EX_MEM;


ARCHITECTURE TypeArchitecture OF EX_MEM IS

SIGNAL exmem_s : std_logic_vector(142 DOWNTO 0);

BEGIN

	PROCESS (clk)
	BEGIN
		IF (rising_edge(clk)) THEN
			exmem_s(31 DOWNTO 0)   <= sumIn;
			exmem_s(32)  <= zeroIn;
			exmem_s(64 DOWNTO 33)  <= aluIn;
			exmem_s(96 DOWNTO 65) <= read2In;
			exmem_s(101 DOWNTO 97) <= wbAddIn;
			exmem_s(104 DOWNTO 102) <= WBin;
			exmem_s(110 DOWNTO 105) <= Min;
			exmem_s(142 downto 111) <= pcPl4In;
		END IF;
		IF (falling_edge(clk)) THEN
			pcOut    <=  exmem_s(31 DOWNTO 0);
			
			if (exmem_s(32) = 'U') then
				zeroOut <= '0';
			else
				zeroOut <= exmem_s(32);
			end if; 

			if (exmem_s(64 DOWNTO 33) = "UUUUUUUUUUUUUUUUUUUUUUUUUUUUUUUU") then
				aluOut <= "00000000000000000000000000000000";
			else
				aluOut <= exmem_s(64 DOWNTO 33);
			end if;
			
			read2Out <= exmem_s(96 DOWNTO 65);
			wbAddOut <= exmem_s(101 DOWNTO 97);
			
			if (exmem_s(109 DOWNTO 105) = "UUUUUU") then
				Mout <= "000000";
			else
				Mout <= exmem_s(110 DOWNTO 105);
			end if;
			
			WBout <= exmem_s(104 DOWNTO 102);

			pcPl4Out <= exmem_s(142 downto 111);
			
			
		END IF;
	END PROCESS;

	
END TypeArchitecture;

// VHDL entity MEM_WB, as the project stores it:
LIBRARY IEEE;
USE ieee.std_logic_1164.all;

ENTITY MEM_WB IS
  PORT (
    clk            : IN  std_logic;                   
    readIn           : IN  std_logic_vector(31 DOWNTO 0);
    aluIn        : IN  std_logic_vector(31 DOWNTO 0);
    wbAddIn        : IN  std_logic_vector(4 downto 0);
    WBin		    : IN  std_logic_vector(2 downto 0);
    pcPl4In	    : IN std_logic_vector(31 downto 0);
    pcPlIIn	    : IN std_logic_vector(31 downto 0);
                        
    readOut         : OUT std_logic_vector(31 DOWNTO 0);
    aluOut	    : OUT std_logic_vector(31 DOWNTO 0);
    wbAddOut       : OUT std_logic_vector(4 downto 0);
    WBout		    : OUT std_logic_vector(2 downto 0);
    pcPl4Out       : OUT std_logic_vector(31 downto 0);
    pcPlIOut	    : Out std_logic_vector(31 downto 0)
    );
END MEM_WB;


ARCHITECTURE TypeArchitecture OF MEM_WB IS

SIGNAL memwb_s : std_logic_vector(135 DOWNTO 0);

BEGIN

	PROCESS (clk)
	BEGIN
		IF (rising_edge(clk)) THEN
			memwb_s(31 DOWNTO 0)   <= readIn;
			memwb_s(63 DOWNTO 32)  <= aluIn;
			memwb_s(68 DOWNTO 64)  <= wbAddIn;
			memwb_s(71 DOWNTO 69)  <= WBin;
			memwb_s(103 downto 72) <= pcPl4In;
			memwb_s(135 downto 104) <= pcPlIIn;
			
		END IF;
		IF (falling_edge(clk)) THEN
			readOut    <=  memwb_s(31 DOWNTO 0);
			aluOut  <=  memwb_s(63 DOWNTO 32);
			wbAddOut <= memwb_s(68 DOWNTO 64);
			WBout <= memwb_s(71 DOWNTO 69);
			pcPl4Out <= memwb_s(103 downto 72);
			pcPlIOut <= memwb_s(135 downto 104);
		END IF;
	END PROCESS;

	
END TypeArchitecture;
