// Logisim project somadorVetorial.circ as structural Verilog
module main (
  input  [31:0] A_i,
  input  [31:0] B_i,
  input  [1:0] vecSize_i,
  input  mode_i,
  output [31:0] S_o
);

  SomadorVetorial somadorvetorial_1 (.A_i(A_i), .B_i(B_i), .vecSize_i(vecSize_i), .mode_i(mode_i), .S_o(S_o));
endmodule

// VHDL entity SomadorVetorial, as the project stores it:
LIBRARY ieee;
USE ieee.std_logic_1164.all;

ENTITY SomadorVetorial IS
	PORT (
		A_i        : IN std_logic_vector(31 downto 0);
		B_i        : IN std_logic_vector(31 downto 0);
		vecSize_i  : IN std_logic_vector(1 downto 0);
		mode_i	 : IN std_logic;
		S_o        : OUT std_logic_vector(31 downto 0)
	);
END SomadorVetorial;

ARCHITECTURE TypeArchitecture OF SomadorVetorial IS
	signal B     : std_logic_vector(31 downto 0);
	signal Carry : std_logic_vector(31 downto 0);
	signal Soma  : std_logic_vector(31 downto 0);

BEGIN
	INVERSORB: for i in 0 to 31 generate
		B(i)   <= B_i(i) xor mode_i;
	end generate INVERSORB;

	Carry(0) <= mode_i;

	GERARCARRY1: for i in 1 to 3 generate
		Carry(i) <= (A_i(i-1) and B(i-1)) or ((A_i(i-1) xor B(i-1)) and Carry(i-1));
	end generate GERARCARRY1;

	Carry(4) <= mode_i when (vecSize_i = "00") else
		(A_i(3) and B(3)) or ((A_i(3) xor B(3)) and Carry(3));

	GERARCARRY2: for i in 5 to 7 generate
		Carry(i) <= (A_i(i-1) and B(i-1)) or ((A_i(i-1) xor B(i-1)) and Carry(i-1));
	end generate GERARCARRY2;

	Carry(8) <= mode_i when (vecSize_i = "00" or vecSize_i = "01") ELSE
		(A_i(7) and B(7)) or ((A_i(7) xor B(7)) and Carry(7));

	GERARCARRY3: for i in 9 to 11 generate
		Carry(i) <= (A_i(i-1) and B(i-1)) or ((A_i(i-1) xor B(i-1)) and Carry(i-1));
	end generate GERARCARRY3;

	Carry(12) <= mode_i when (vecSize_i = "00") ELSE
		(A_i(11) and B(11)) or ((A_i(11) xor B(11)) and Carry(11));

	GERARCARRY4: for i in 13 to 15 generate
		Carry(i) <= (A_i(i-1) and B(i-1)) or ((A_i(i-1) xor B(i-1)) and Carry(i-1));
	end generate GERARCARRY4;

	Carry(16) <= mode_i when (vecSize_i = "00" or vecSize_i = "01" or vecSize_i = "10") ELSE
		(A_i(15) and B(15)) or ((A_i(15) xor B(15)) and Carry(15));

	GERARCARRY5: for i in 17 to 19 generate
		Carry(i) <= (A_i(i-1) and B(i-1)) or ((A_i(i-1) xor B(i-1)) and Carry(i-1));
	end generate GERARCARRY5;

	Carry(20) <= mode_i when (vecSize_i = "00") else
		(A_i(19) and B(19)) or ((A_i(19) xor B(19)) and Carry(19));

	GERARCARRY6: for i in 21 to 23 generate
		Carry(i) <= (A_i(i-1) and B(i-1)) or ((A_i(i-1) xor B(i-1)) and Carry(i-1));
	end generate GERARCARRY6;

	Carry(24) <= mode_i when (vecSize_i = "00" or vecSize_i = "01") else
		(A_i(23) and B(23)) or ((A_i(23) xor B(23)) and Carry(23));

	GERARCARRY7: for i in 25 to 27 generate
		Carry(i) <= (A_i(i-1) and B(i-1)) or ((A_i(i-1) xor B(i-1)) and Carry(i-1));
	end generate GERARCARRY7;

	Carry(28) <= mode_i when (vecSize_i = "00") else
		(A_i(27) and B(27)) or ((A_i(27) xor B(27)) and Carry(27));

	GERARCARRY8: for i in 29 to 31 generate
		Carry(i) <= (A_i(i-1) and B(i-1)) or ((A_i(i-1) xor B(i-1)) and Carry(i-1));
	end generate GERARCARRY8;

	GERARSOMA: for i in 0 to 31 generate
		Soma(i) <= A_i(i) xor B(i) xor Carry(i);
	end generate GERARSOMA;

	S_o <= Soma;

END TypeArchitecture;
